// Digital circuit apresentacao.dig as structural Verilog
module apresentacao (
);

  flip_flop_d_ck0 flip_flop_d_ck0_1 ();  // open: ck, D, Q, nQ
  flip_flop_d_s0_r0_ck0_contador_1bit flip_flop_d_s0_r0_ck0_contador_1bit_1 ();  // open: nS, nR, ck, Q, nQ
  flip_flop_d_s0_r0_ck0_contador_4bits flip_flop_d_s0_r0_ck0_contador_4bits_1 ();  // open: nMS, nMR, ck, Q0, Q1, Q2, Q3
  // _7474 _7474_1: pin names not known
  // _7474 _7474_2: pin names not known
  flip_flop_d_ck0_contador_1bit flip_flop_d_ck0_contador_1bit_1 ();  // open: ck, Q, nQ
  flip_flop_d_s0_r0_ck0_contador_2bits flip_flop_d_s0_r0_ck0_contador_2bits_1 ();  // open: nS, nR, ck, Q0, Q1
  contador_assincrono contador_assincrono_1 ();  // open: ck, nMR, Q0, Q1, Q2, Q3, Q0_Q4

  // Notes on the sheet:
  //   74HC74
  //   http://pdf.datasheetcatalog.com/datasheet/on_semiconductor2/74HC74.PDF
endmodule
